# Fritzing sketch Sumo (saved by Fritzing 0.9.3b)

parts:
  Part1 = Arduino Nano (Rev3.0)
  U1 = DRV8833
  M1 = DC Motor
  M2 = DC Motor
  U2 = LIPO-1000mAh [package=lipo-1000]
  Part4 = GP2Y0D810Z0F
  Part5 = GP2Y0D810Z0F
  Part6 = GP2Y0D810Z0F
  Part7 = GP2Y0D810Z0F
  Part8 = GP2Y0D810Z0F

nets:
  N1: Part1.GND, U1.GND#0
  N2: Part1.D3, U1.AOUT2
  N3: Part1.D9, U1.BOUT1
  N4: Part1.D10, U1.BOUT2
  N5: Part1.D11/MOSI, U1.AOUT1
  VIN: Part1.VIN, U1.VIN, U2.+
  N6: Part1.A4, Part4.VO
  N7: Part1.A3, Part5.VO
  N8: Part1.A2, Part6.VO
  N9: Part1.A1, Part7.VO
  N10: Part1.A0, Part8.VO
  N11: U1.BIN1, M1.pin_1
  N12: U1.BIN2, M1.pin_2
  N13: U1.AIN2, M2.pin_2
  N14: U1.AIN1, M2.pin_1
  N15: U1.GND#8, U2.-

notes:
  qtr-1cr Izquierdo
  qtr-1cr Derecho
  Izquierdo
  Centro
  -Izquierdo
  -centro
  -Derecho
  Derecho
  Motor2
  Motor1
  grn
  Vin

custom parts:
  DRV8833: The DRV8833 provides a dual bridge motor driver solution for toys, printers, and other mechatronic applications.
